# Fritzing sketch cestus (saved by Fritzing 0.9.3b)
circuit board: 10.7088cm x 12.5795cm

parts:
  Part2 = Flora LSM9DS0 9DOF [part_number=LSM9DS0]
  Part3 = Adafruit Flora [part_number="Adafruit #659"]
  Part4 = 16 NeoPixel Ring [part_number=1463]

nets:
  GND: Part2.GND, Part3.GND, Part4.GND
  N1: Part2.SCL, Part3.IO2/SDA
  N2: Part2.SDA, Part3.IO3/SCL
  3.3V: Part2.3.3V, Part3.+3V3
  N3: Part3.IO6, Part4.IN
  N4: Part3.VBAT, Part4.VDD

notes:
  Adafruit LSM9DS0 sensor
  Adafruit Flora system board
  Adafruit NeoPixel 16-LED ring

custom parts:
  Flora LSM9DS0 9DOF: Add motion, direction and orientation sensing to your wearable FLORA project with this high precision 9-DOF sensors. Inside are three sensors, one is a classic 3-axis accelerometer, which can tell you which direction is down towards the Earth (by measuring gravity) or how fast the board is accelerating in 3D space. The other is a 3-axis magnetometer that can sense where the strongest magnetic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
  Adafruit Flora: FLORA is Adafruit's fully-featured wearable electronics platform. It's a round, sewable, Arduino-compatible microcontroller designed to empower amazing wearables projects. The FLORA is small (1.75" diameter, weighing 4.4 grams). The FLORA has built-in USB support. Built in USB means you plug it in to program it, it just shows up - all you need is a Micro-B USB cable, no additional purchases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
  16 NeoPixel Ring: 16 ultra bright smart LED NeoPixels are arranged in a circle with 1.75" (44.5mm) outer diameter. The rings are 'chainable' - connect the output pin of one to the input pin of another. Use only one microcontroller pin to control as many as you can chain together! Each LED is addressable as the driver chip is inside the LED. Each one has ~18mA constant current drive so the color will be very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
